// Logisim project Projet.circ as structural Verilog: 5 circuits, main circuit main
module main (
);

  Registre_4_bits registre_4_bits_1 ();  // open: in_5, in_1, in_2, in_3, in_4
  Registre_4_bits registre_4_bits_2 ();  // open: in_5, in_1, in_2, in_3, in_4
endmodule

module RS (
  input  R,
  input  S,
  output Q
);

  wire nor_1_out;

  nor nor_1 (nor_1_out, R, Q);
  nor nor_2 (Q, nor_1_out, S);
endmodule

// REG4
module Registre_4_bits (
  input  in_1,
  input  in_2,
  input  in_3,
  input  in_4,
  input  in_5
);

  wire rs_1_q, rs_2_q, rs_3_q, rs_4_q;

  RS rs_1 (.R(in_4), .S(in_5), .Q(rs_1_q));
  RS rs_2 (.R(in_3), .S(in_5), .Q(rs_2_q));
  RS rs_3 (.R(in_2), .S(in_5), .Q(rs_3_q));
  RS rs_4 (.R(in_1), .S(in_5), .Q(rs_4_q));
  LED led_1 (.in(rs_1_q));
  LED led_2 (.in(rs_2_q));
  LED led_3 (.in(rs_3_q));
  LED led_4 (.in(rs_4_q));
endmodule

module Full_adder (
  input  A,
  input  B,
  input  Cin,
  output S,
  output Cout
);

  wire and_1_out, and_2_out, xor_1_out;

  xor xor_1 (xor_1_out, A, B);
  xor xor_2 (S, xor_1_out, Cin);
  and and_1 (and_1_out, xor_1_out, Cin);
  buf and_2 (and_2_out, A);  // AND_Gate
  or or_1 (Cout, and_1_out, and_2_out);
endmodule

module Mux_4 (
  input  selA,
  input  selB,
  input  A,
  input  B,
  input  C,
  input  D,
  output Q
);

  wire and_1_out, and_2_out, and_3_out, and_4_out, not_1_out, not_2_out;

  not not_1 (not_1_out, selA);
  not not_2 (not_2_out, selB);
  and and_1 (and_1_out, A, not_2_out, not_1_out);
  and and_2 (and_2_out, B, not_2_out, selA);
  and and_3 (and_3_out, C, not_1_out, selB);
  and and_4 (and_4_out, D, selB, selA);
  or or_1 (Q, and_1_out, and_2_out, and_3_out, and_4_out);
endmodule
